// Logisim project 8_to_1_mux.circ as structural Verilog: 1 circuit, main circuit eight_to_one_mux
module eight_to_one_mux (
  input  [7:0] A,
  input  [2:0] S,
  output Y
);

  wire nand_1_out, nand_2_out, nand_3_out, nand_4_out, nand_5_out, nand_6_out, nand_7_out, nand_8_out,
       nand_9_out, nand_10_out, nand_11_out;

  nand nand_1 (nand_1_out, S[0], S[0]);
  nand nand_2 (nand_2_out, S[1], S[1]);
  nand nand_3 (nand_3_out, S[2], S[2]);
  nand nand_4 (nand_4_out, A[0], nand_1_out, nand_2_out, nand_3_out);
  nand nand_5 (nand_5_out, A[1], S[0], nand_2_out, nand_3_out);
  nand nand_6 (nand_6_out, A[2], nand_1_out, S[1], nand_3_out);
  nand nand_7 (nand_7_out, A[3], S[0], S[1], nand_3_out);
  nand nand_8 (nand_8_out, A[4], nand_1_out, nand_2_out, S[2]);
  nand nand_9 (nand_9_out, A[5], S[0], nand_2_out, S[2]);
  nand nand_10 (nand_10_out, A[6], nand_1_out, S[1], S[2]);
  nand nand_11 (nand_11_out, A[7], S[0], S[1], S[2]);
  nand nand_12 (Y, nand_4_out, nand_5_out, nand_6_out, nand_7_out, nand_8_out, nand_9_out, nand_10_out, nand_11_out);
endmodule
