// Logisim project ALU.circ as structural Verilog: 8 circuits, main circuit Eight_or
module Eight_or (
  input  S,
  input  [7:0] B,
  input  [7:0] A,
  output [7:0] Y
);

  wire and_1_out, and_2_out, and_3_out, and_4_out, and_5_out, and_6_out, and_7_out, and_8_out, or_1_out,
       or_2_out, or_3_out, or_4_out, or_5_out, or_6_out, or_7_out, or_8_out;

  and and_1 (and_1_out, A[0], B[0]);
  and and_2 (and_2_out, A[1], B[1]);
  and and_3 (and_3_out, A[2], B[2]);
  and and_4 (and_4_out, A[3], B[3]);
  and and_5 (and_5_out, A[4], B[4]);
  and and_6 (and_6_out, A[5], B[5]);
  and and_7 (and_7_out, A[6], B[6]);
  and and_8 (and_8_out, B[7], A[7]);
  or or_1 (or_1_out, A[0], B[0]);
  or or_2 (or_2_out, A[1], B[1]);
  or or_3 (or_3_out, A[2], B[2]);
  or or_4 (or_4_out, A[3], B[3]);
  or or_5 (or_5_out, A[4], B[4]);
  or or_6 (or_6_out, A[5], B[5]);
  or or_7 (or_7_out, A[6], B[6]);
  or or_8 (or_8_out, A[7], B[7]);
  Multiplexer multiplexer_1 (.in0(or_1_out), .in1(and_1_out), .out(Y[0]), .sel(S));
  Multiplexer multiplexer_2 (.in0(or_2_out), .in1(and_2_out), .out(Y[1]), .sel(S));
  Multiplexer multiplexer_3 (.in0(or_3_out), .in1(and_3_out), .out(Y[2]), .sel(S));
  Multiplexer multiplexer_4 (.in0(or_4_out), .in1(and_4_out), .out(Y[3]), .sel(S));
  Multiplexer multiplexer_5 (.in0(or_5_out), .in1(and_5_out), .out(Y[4]), .sel(S));
  Multiplexer multiplexer_6 (.in0(or_6_out), .in1(and_6_out), .out(Y[5]), .sel(S));
  Multiplexer multiplexer_7 (.in0(or_7_out), .in1(and_7_out), .out(Y[6]), .sel(S));
  Multiplexer multiplexer_8 (.in0(or_8_out), .in1(and_8_out), .out(Y[7]), .sel(S));
endmodule

module Eight_to_one_eight_bit (
  input  [7:0] D7,
  input  [7:0] D6,
  input  [7:0] D5,
  input  [7:0] D4,
  input  [7:0] D3,
  input  [7:0] D2,
  input  [7:0] D1,
  input  [7:0] D0,
  input  [2:0] S,
  output [7:0] Y
);

  eight_to_one_mux eight_to_one_mux_1 (.A({D7[0], D6[0], D5[0], D4[0], D3[0], D2[0], D1[0], D0[0]}), .S(S), .Y(Y[0]));
  eight_to_one_mux eight_to_one_mux_2 (.A({D7[1], D6[1], D5[1], D4[1], D3[1], D2[1], D1[1], D0[1]}), .S(S), .Y(Y[1]));
  eight_to_one_mux eight_to_one_mux_3 (.A({D7[2], D6[2], D5[2], D4[2], D3[2], D2[2], D1[2], D0[2]}), .S(S), .Y(Y[2]));
  eight_to_one_mux eight_to_one_mux_4 (.A({D7[3], D6[3], D5[3], D4[3], D3[3], D2[3], D1[3], D0[3]}), .S(S), .Y(Y[3]));
  eight_to_one_mux eight_to_one_mux_5 (.A({D7[4], D6[4], D5[4], D4[4], D3[4], D2[4], D1[4], D0[4]}), .S(S), .Y(Y[4]));
  eight_to_one_mux eight_to_one_mux_6 (.A({D7[5], D6[5], D5[5], D4[5], D3[5], D2[5], D1[5], D0[5]}), .S(S), .Y(Y[5]));
  eight_to_one_mux eight_to_one_mux_7 (.A({D7[6], D6[6], D5[6], D4[6], D3[6], D2[6], D1[6], D0[6]}), .S(S), .Y(Y[6]));
  eight_to_one_mux eight_to_one_mux_8 (.A({D7[7], D6[7], D5[7], D4[7], D3[7], D2[7], D1[7], D0[7]}), .S(S), .Y(Y[7]));
endmodule

module ALU (
  input  [2:0] Control,
  input  [7:0] B,
  input  [7:0] A,
  output [7:0] Y,
  output Overflow,
  output Equal,
  output Sign
);

  wire [7:0] arthright_1_y, eight_or_1_y, leftshift_1_y, not_1_out, shift_right_1_y, sub_1_diff;

  arthright arthright_1 (.A(A), .Shamt(B[2:0]), .Y(arthright_1_y));
  Shift_right shift_right_1 (.A(A), .Shamt(B[2:0]), .Y(shift_right_1_y));
  leftshift leftshift_1 (.A(A), .Shamt(B[2:0]), .Y(leftshift_1_y));
  sub sub_1 (.B(B), .S(Control[0]), .A(A), .Diff(sub_1_diff), .OFflag(Overflow));
  equality equality_1 (.A(A), .B(B), .out_3(Equal));
  Eight_or eight_or_1 (.S(Control[0]), .B(B), .A(A), .Y(eight_or_1_y));
  and and_1 (Sign, Control[0], sub_1_diff[7]);
  assign not_1_out = ~A;  // NOT_Gate not_1, 8 bits wide
  Eight_to_one_eight_bit eight_to_one_eight_bit_1 (
    .D7(eight_or_1_y), .D6(eight_or_1_y), .D5(not_1_out), .D4(arthright_1_y), .D3(shift_right_1_y),
    .D2(leftshift_1_y), .D1(sub_1_diff), .D0(sub_1_diff), .S(Control), .Y(Y));
endmodule

module CPU (
);

  wire and_9_out, and_10_out, and_11_out, and_12_out, and_13_out, and_14_out, and_15_out, and_16_out,
       and_17_out, and_18_out, and_19_out, and_20_out, and_21_out, and_22_out, and_23_out, and_24_out,
       clock_1_out, control_unit_1_accum_read, control_unit_1_accum_write, control_unit_1_b_write,
       control_unit_1_dest_write, control_unit_1_source1_read, control_unit_1_source2_read, nor_1_out;
  wire [1:0] sequencer_fsm_1_y0;
  wire [2:0] control_unit_1_aluop;
  wire [7:0] Accumulator_q, alu_1_y, and_1_out, B_q, control_unit_1_dest, control_unit_1_source1,
       control_unit_1_source2, controlled_buffer_1_out, Gen0_q, Gen1_q, Gen2_q, R0_bus_write_out;
  wire [15:0] adder_1_out, Ins_reg_q, Program_Counter_q, rom_1_data;

  Clock clock_1 (.out(clock_1_out));
  Register Gen0 (.D(controlled_buffer_1_out), .en(and_1_out[0]), .clk(clock_1_out), .Q(Gen0_q));  // open: clr
  Register Gen1 (.D(controlled_buffer_1_out), .en(and_1_out[1]), .clk(clock_1_out), .Q(Gen1_q));  // open: clr
  Register Gen2 (.D(controlled_buffer_1_out), .en(and_1_out[2]), .clk(clock_1_out), .Q(Gen2_q));  // open: clr
  Register B (.D(controlled_buffer_1_out), .en(control_unit_1_b_write), .clk(clock_1_out), .Q(B_q));  // open: clr
  assign controlled_buffer_1_out = R0_bus_write_out[0] ? Gen0_q : 8'bz;  // Controlled_Buffer controlled_buffer_1
  assign controlled_buffer_1_out = R0_bus_write_out[1] ? Gen1_q : 8'bz;  // Controlled_Buffer controlled_buffer_2
  assign controlled_buffer_1_out = R0_bus_write_out[7] ? Gen2_q : 8'bz;  // Controlled_Buffer controlled_buffer_3
  and and_1 (and_1_out[0], control_unit_1_dest_write, control_unit_1_dest[0]);
  sequencer_fsm sequencer_fsm_1 (.Clock(clock_1_out), .Y0(sequencer_fsm_1_y0[0]), .Y1(sequencer_fsm_1_y0[1]));
  and and_2 (and_1_out[1], control_unit_1_dest_write, control_unit_1_dest[1]);
  ALU alu_1 (
    .Control(control_unit_1_aluop), .B(B_q), .A(controlled_buffer_1_out), .Y(alu_1_y));  // open: Overflow, Equal, Sign
  nor nor_1 (nor_1_out, sequencer_fsm_1_y0[0], sequencer_fsm_1_y0[1]);
  and and_3 (and_1_out[2], control_unit_1_dest_write, control_unit_1_dest[2]);
  and and_4 (and_1_out[3], control_unit_1_dest_write, control_unit_1_dest[3]);
  and and_5 (and_1_out[4], control_unit_1_dest_write, control_unit_1_dest[4]);
  Register Accumulator (
    .D(alu_1_y), .en(control_unit_1_accum_write), .clk(clock_1_out), .Q(Accumulator_q));  // open: clr
  Register #(.width(16)) Program_Counter (
    .D(adder_1_out), .en(1'b1), .clk(nor_1_out), .Q(Program_Counter_q));  // open: clr
  Adder #(.width(16)) adder_1 (.a(Program_Counter_q), .b(16'h1), .out(adder_1_out));  // open: cin, cout
  Register #(.width(16)) Ins_reg (.D(rom_1_data), .en(1'b1), .clk(nor_1_out), .Q(Ins_reg_q));  // open: clr
  and and_6 (and_1_out[5], control_unit_1_dest_write, control_unit_1_dest[5]);
  and and_7 (and_1_out[6], control_unit_1_dest_write, control_unit_1_dest[6]);
  assign controlled_buffer_1_out = control_unit_1_accum_read ? Accumulator_q : 8'bz;  // Controlled_Buffer controlled_buffer_4
  Control_unit control_unit_1 (
    .Insruction(Ins_reg_q), .Instruction_step(sequencer_fsm_1_y0), .Source1(control_unit_1_source1),
    .Source2(control_unit_1_source2), .Dest(control_unit_1_dest), .ALUop(control_unit_1_aluop),
    .Source1_Read(control_unit_1_source1_read), .B_write(control_unit_1_b_write),
    .Source2_Read(control_unit_1_source2_read), .Accum_Write(control_unit_1_accum_write),
    .Accum_Read(control_unit_1_accum_read), .Dest_Write(control_unit_1_dest_write));
  and and_8 (and_1_out[7], control_unit_1_dest_write, control_unit_1_dest[7]);
  ROM #(.addrWidth(16), .dataWidth(16)) rom_1 (.addr(Program_Counter_q), .data(rom_1_data));
  and and_9 (and_9_out, control_unit_1_source1[0], control_unit_1_source1_read);
  and and_10 (and_10_out, control_unit_1_source1[1], control_unit_1_source1_read);
  and and_11 (and_11_out, control_unit_1_source1[2], control_unit_1_source1_read);
  and and_12 (and_12_out, control_unit_1_source1[3], control_unit_1_source1_read);
  and and_13 (and_13_out, control_unit_1_source1[4], control_unit_1_source1_read);
  and and_14 (and_14_out, control_unit_1_source1[5], control_unit_1_source1_read);
  and and_15 (and_15_out, control_unit_1_source1[6], control_unit_1_source1_read);
  and and_16 (and_16_out, control_unit_1_source1[7], control_unit_1_source1_read);
  and and_17 (and_17_out, control_unit_1_source2[0], control_unit_1_source2_read);
  and and_18 (and_18_out, control_unit_1_source2[1], control_unit_1_source2_read);
  and and_19 (and_19_out, control_unit_1_source2[2], control_unit_1_source2_read);
  and and_20 (and_20_out, control_unit_1_source2[3], control_unit_1_source2_read);
  and and_21 (and_21_out, control_unit_1_source2[4], control_unit_1_source2_read);
  and and_22 (and_22_out, control_unit_1_source2[5], control_unit_1_source2_read);
  and and_23 (and_23_out, control_unit_1_source2[6], control_unit_1_source2_read);
  and and_24 (and_24_out, control_unit_1_source2[7], control_unit_1_source2_read);
  or R0_bus_write (R0_bus_write_out[0], and_9_out, and_17_out);
  or R1_bus_write (R0_bus_write_out[1], and_10_out, and_18_out);
  or R2_bus_write (R0_bus_write_out[7], and_11_out, and_19_out);
  or R3_bus_write (R0_bus_write_out[7], and_12_out, and_20_out);
  or R4_bus_write (R0_bus_write_out[7], and_13_out, and_21_out);
  or R5_bus_write (R0_bus_write_out[7], and_14_out, and_22_out);
  or R6_bus_write (R0_bus_write_out[7], and_15_out, and_23_out);
  or R7_bus_write (R0_bus_write_out[7], and_16_out, and_24_out);
  RAM #(.addrWidth(16)) ram_1 ();  // open: addr, we, oe, clk, din, dout

  // Notes on the sheet:
  //   Register_read_enable_bus
  //   contents of rom_1 (hex, n*v repeats v):
  //   40
  //   Register_write_enable_bus
endmodule

module Control_unit (
  input  [15:0] Insruction,
  input  [1:0] Instruction_step,
  output [7:0] Source1,
  output [7:0] Source2,
  output [7:0] Dest,
  output [2:0] ALUop,
  output Source1_Read,
  output B_write,
  output Source2_Read,
  output Accum_Write,
  output Accum_Read,
  output Dest_Write
);

  wire add_ctrl_1_accum_bus_write, add_ctrl_1_accum_write_enable, add_ctrl_1_b_write_enable,
       add_ctrl_1_dr_write_enable, add_ctrl_1_sr1_bus_write, add_ctrl_1_sr2_bus_write;

  Add_ctrl add_ctrl_1 (
    .Ins_step(Instruction_step), .SR1_bus_write(add_ctrl_1_sr1_bus_write),
    .B_write_enable(add_ctrl_1_b_write_enable), .SR2_bus_write(add_ctrl_1_sr2_bus_write),
    .Accum_write_enable(add_ctrl_1_accum_write_enable), .Accum_bus_write(add_ctrl_1_accum_bus_write),
    .DR_write_enable(add_ctrl_1_dr_write_enable));
  Multiplexer #(.select(4)) multiplexer_1 (
    .in0(add_ctrl_1_sr1_bus_write), .out(Source1_Read), .sel(Insruction[15:12]));  // open: in1, in2, in3, in4, in5, in6, in7, in8, in9, in10, in11, in12, in13, in14, in15
  Multiplexer #(.select(4)) multiplexer_2 (
    .in0(add_ctrl_1_b_write_enable), .out(B_write), .sel(Insruction[15:12]));  // open: in1, in2, in3, in4, in5, in6, in7, in8, in9, in10, in11, in12, in13, in14, in15
  Multiplexer #(.select(4)) multiplexer_3 (
    .in0(add_ctrl_1_sr2_bus_write), .out(Source2_Read), .sel(Insruction[15:12]));  // open: in1, in2, in3, in4, in5, in6, in7, in8, in9, in10, in11, in12, in13, in14, in15
  Multiplexer #(.select(4)) multiplexer_4 (
    .in0(add_ctrl_1_accum_write_enable), .out(Accum_Write), .sel(Insruction[15:12]));  // open: in1, in2, in3, in4, in5, in6, in7, in8, in9, in10, in11, in12, in13, in14, in15
  Multiplexer #(.select(4)) multiplexer_5 (
    .in0(add_ctrl_1_accum_bus_write), .out(Accum_Read), .sel(Insruction[15:12]));  // open: in1, in2, in3, in4, in5, in6, in7, in8, in9, in10, in11, in12, in13, in14, in15
  Multiplexer #(.select(4)) multiplexer_6 (
    .in0(add_ctrl_1_dr_write_enable), .out(Dest_Write), .sel(Insruction[15:12]));  // open: in1, in2, in3, in4, in5, in6, in7, in8, in9, in10, in11, in12, in13, in14, in15
  Register_decoder SR1 (
    .Sel(Insruction[11:9]), .R0(Source1[0]), .R1(Source1[1]), .R2(Source1[2]), .R3(Source1[3]),
    .R4(Source1[4]), .R5(Source1[5]), .R6(Source1[6]), .R7(Source1[7]));
  Register_decoder SR2 (
    .Sel(Insruction[8:6]), .R0(Source2[0]), .R1(Source2[1]), .R2(Source2[2]), .R3(Source2[3]),
    .R4(Source2[4]), .R5(Source2[5]), .R6(Source2[6]), .R7(Source2[7]));
  Register_decoder DR (
    .Sel(Insruction[5:3]), .R0(Dest[0]), .R1(Dest[1]), .R2(Dest[2]), .R3(Dest[3]), .R4(Dest[4]),
    .R5(Dest[5]), .R6(Dest[6]), .R7(Dest[7]));

  assign ALUop = Insruction[14:12];

  // Notes on the sheet:
  //   SR_bus_write
endmodule

module sequencer_fsm (
  input  Clock,
  output Y0,
  output Y1
);

  wire and_1_out, and_2_out, nor_1_out, not_1_out, not_2_out;
  wire [1:0] or_2_out;

  and and_1 (and_1_out, Y0, not_2_out);
  and and_2 (and_2_out, not_1_out, Y1);
  nor nor_1 (nor_1_out, Y0, Y1);
  or or_1 (or_2_out[1], and_1_out, and_2_out);
  or or_2 (or_2_out[0], and_2_out, nor_1_out);
  Register #(.width(2)) register_1 (.D(or_2_out), .en(1'b1), .clk(Clock), .Q({Y1, Y0}));  // open: clr
  not not_1 (not_1_out, Y0);
  not not_2 (not_2_out, Y1);
endmodule

module Register_decoder (
  input  [2:0] Sel,
  output R0,
  output R1,
  output R2,
  output R3,
  output R4,
  output R5,
  output R6,
  output R7
);

  wire not_1_out, not_2_out, not_3_out;

  not not_1 (not_1_out, Sel[0]);
  not not_2 (not_2_out, Sel[1]);
  not not_3 (not_3_out, Sel[2]);
  and and_1 (R0, not_3_out, not_2_out, not_1_out);
  and and_2 (R1, not_3_out, not_2_out, Sel[0]);
  and and_3 (R2, not_3_out, Sel[1], not_1_out);
  and and_4 (R3, not_3_out, Sel[1], Sel[0]);
  and and_5 (R4, Sel[2], not_2_out, not_1_out);
  and and_6 (R5, Sel[2], not_2_out, Sel[0]);
  and and_7 (R6, Sel[2], Sel[1], not_1_out);
  and and_8 (R7, Sel[2], Sel[1], Sel[0]);
endmodule

module Add_ctrl (
  input  [1:0] Ins_step,
  output SR1_bus_write,
  output B_write_enable,
  output SR2_bus_write,
  output Accum_write_enable,
  output Accum_bus_write,
  output DR_write_enable
);

  wire not_1_out, not_2_out;

  not not_1 (not_1_out, Ins_step[1]);
  not not_2 (not_2_out, Ins_step[0]);
  nor nor_1 (B_write_enable, Ins_step[0], Ins_step[1]);
  and and_1 (Accum_write_enable, not_1_out, Ins_step[0]);
  and and_2 (Accum_bus_write, not_2_out, Ins_step[1]);

  assign DR_write_enable = Accum_bus_write;
  assign SR1_bus_write = B_write_enable;
  assign SR2_bus_write = Accum_write_enable;
endmodule
