// Logisim project CLA.circ as structural Verilog: 2 circuits, main circuit CLA_four_bit_block
module CLA_four_bit_block (
  input  Cin,
  input  A0,
  input  A1,
  input  A2,
  input  A3,
  input  B0,
  input  B1,
  input  B2,
  input  B3,
  output S0,
  output S1,
  output S2,
  output S3,
  output Cout
);

  wire and_1_out, and_2_out, and_3_out, and_4_out, and_5_out, and_6_out, fulladder_1_cout, fulladder_2_cout,
       fulladder_3_cout, fulladder_4_cout, G0_out, G1_out, G2_out, G3_out, Gi_j_out, or_2_out, or_3_out,
       P0_out, P1_out, P2_out, P3_out, Pi_j_out;

  and and_1 (and_1_out, P3_out, and_3_out);
  and and_2 (and_2_out, P1_out, P0_out);
  and and_3 (and_3_out, P2_out, and_2_out);
  and Pi_j (Pi_j_out, and_1_out, Cin);
  and G3 (G3_out, B3, A3);
  or P3 (P3_out, B3, A3);
  or Gi_j (Gi_j_out, G3_out, and_4_out);
  or or_1 (Cout, Pi_j_out, Gi_j_out);
  and G2 (G2_out, B2, A2);
  or P2 (P2_out, B2, A2);
  or or_2 (or_2_out, G2_out, and_5_out);
  and and_4 (and_4_out, P3_out, or_2_out);
  and G1 (G1_out, B1, A1);
  and and_5 (and_5_out, P2_out, or_3_out);
  or P1 (P1_out, B1, A1);
  or or_3 (or_3_out, G1_out, and_6_out);
  and G0 (G0_out, B0, A0);
  or P0 (P0_out, B0, A0);
  and and_6 (and_6_out, G0_out, P1_out);
  fulladder fulladder_1 (.A(A0), .B(B0), .Cin(Cin), .Sum(S0), .Cout(fulladder_1_cout));
  fulladder fulladder_2 (.A(A1), .B(B1), .Cin(fulladder_1_cout), .Sum(S1), .Cout(fulladder_2_cout));
  fulladder fulladder_3 (.A(A2), .B(B2), .Cin(fulladder_2_cout), .Sum(S2), .Cout(fulladder_3_cout));
  fulladder fulladder_4 (.A(A3), .B(B3), .Cin(fulladder_3_cout), .Sum(S3), .Cout(fulladder_4_cout));
  // also tied to GND on the sheet: fulladder_4_cout
endmodule

module CLA (
  input  Cin,
  input  A0,
  input  A1,
  input  A2,
  input  A3,
  input  B0,
  input  B1,
  input  B2,
  input  B3,
  input  A4,
  input  A5,
  input  A6,
  input  A7,
  input  B4,
  input  B5,
  input  B6,
  input  B7,
  output S0,
  output S1,
  output S2,
  output S3,
  output S4,
  output S5,
  output S6,
  output S7,
  output OverflowFlag
);

  wire cla_four_bit_block_1_cout;

  CLA_four_bit_block cla_four_bit_block_1 (
    .Cin(Cin), .A0(A0), .A1(A1), .A2(A2), .A3(A3), .B0(B0), .B1(B1), .B2(B2), .B3(B3), .S0(S0), .S1(S1),
    .S2(S2), .S3(S3), .Cout(cla_four_bit_block_1_cout));
  CLA_four_bit_block cla_four_bit_block_2 (
    .Cin(cla_four_bit_block_1_cout), .A0(A4), .A1(A5), .A2(A6), .A3(A7), .B0(B4), .B1(B5), .B2(B6), .B3(B7),
    .S0(S4), .S1(S5), .S2(S6), .S3(S7), .Cout(OverflowFlag));
endmodule
