// Logisim project chainedadder.circ as structural Verilog: 1 circuit, main circuit main
module main (
  input  a1,
  input  a2,
  input  b1,
  input  b2,
  output S1,
  output S2,
  output Cout2
);

  wire fulladder_1_cout;

  fulladder fulladder_1 (.A(a1), .B(b1), .Cin(1'b0), .Sum(S1), .Cout(fulladder_1_cout));
  fulladder fulladder_2 (.A(a2), .B(b2), .Cin(fulladder_1_cout), .Sum(S2), .Cout(Cout2));
endmodule
