// Logisim project fulladder.circ as structural Verilog: 1 circuit, main circuit fulladder
module fulladder (
  input  A,
  input  B,
  input  Cin,
  output Sum,
  output Cout
);

  wire and_1_out, and_2_out, or_2_out, xor_1_out;

  xor xor_1 (xor_1_out, Cin, B);
  xor xor_2 (Sum, xor_1_out, A);
  and and_1 (and_1_out, B, A);
  or or_1 (Cout, and_1_out, and_2_out);
  or or_2 (or_2_out, B, A);
  and and_2 (and_2_out, Cin, or_2_out);
endmodule
