// Logisim project arthright.circ as structural Verilog: 1 circuit, main circuit arthright
module arthright (
  input  [7:0] A,
  input  [2:0] Shamt,
  output [7:0] Y
);

  eight_to_one_mux eight_to_one_mux_1 (.A({8{A[7]}}), .S(Shamt), .Y(Y[7]));
  eight_to_one_mux eight_to_one_mux_2 (.A({{7{A[7]}}, A[6]}), .S(Shamt), .Y(Y[6]));
  eight_to_one_mux eight_to_one_mux_3 (.A({{6{A[7]}}, A[6:5]}), .S(Shamt), .Y(Y[5]));
  eight_to_one_mux eight_to_one_mux_4 (.A({{5{A[7]}}, A[6:4]}), .S(Shamt), .Y(Y[4]));
  eight_to_one_mux eight_to_one_mux_5 (.A({{4{A[7]}}, A[6:3]}), .S(Shamt), .Y(Y[3]));
  eight_to_one_mux eight_to_one_mux_6 (.A({{3{A[7]}}, A[6:2]}), .S(Shamt), .Y(Y[2]));
  eight_to_one_mux eight_to_one_mux_7 (.A({{2{A[7]}}, A[6:1]}), .S(Shamt), .Y(Y[1]));
  eight_to_one_mux eight_to_one_mux_8 (.A(A), .S(Shamt), .Y(Y[0]));
endmodule
