// Logisim project rightshift.circ as structural Verilog: 1 circuit, main circuit Shift_right
module Shift_right (
  input  [7:0] A,
  input  [2:0] Shamt,
  output [7:0] Y
);

  eight_to_one_mux eight_to_one_mux_1 (.A({{7{1'b0}}, A[7]}), .S(Shamt), .Y(Y[7]));
  eight_to_one_mux eight_to_one_mux_2 (.A({{6{1'b0}}, A[7:6]}), .S(Shamt), .Y(Y[6]));
  eight_to_one_mux eight_to_one_mux_3 (.A({{5{1'b0}}, A[7:5]}), .S(Shamt), .Y(Y[5]));
  eight_to_one_mux eight_to_one_mux_4 (.A({4'b0000, A[7:4]}), .S(Shamt), .Y(Y[4]));
  eight_to_one_mux eight_to_one_mux_5 (.A({3'b000, A[7:3]}), .S(Shamt), .Y(Y[3]));
  eight_to_one_mux eight_to_one_mux_6 (.A({2'b00, A[7:2]}), .S(Shamt), .Y(Y[2]));
  eight_to_one_mux eight_to_one_mux_7 (.A({1'b0, A[7:1]}), .S(Shamt), .Y(Y[1]));
  eight_to_one_mux eight_to_one_mux_8 (.A(A), .S(Shamt), .Y(Y[0]));
endmodule
