// Logisim project sub.circ as structural Verilog: 1 circuit, main circuit sub
module sub (
  input  [7:0] B,
  input  S,
  input  [7:0] A,
  output [7:0] Diff,
  output OFflag
);

  wire cla_1_overflowflag, not_2_out;
  wire [7:0] multiplexer_1_out, not_1_out;

  assign not_1_out = ~B;  // NOT_Gate not_1, 8 bits wide
  Multiplexer #(.width(8)) multiplexer_1 (.in0(B), .in1(not_1_out), .out(multiplexer_1_out), .sel(S));
  not not_2 (not_2_out, S);
  CLA cla_1 (
    .Cin(S), .A0(A[0]), .A1(A[1]), .A2(A[2]), .A3(A[3]), .B0(multiplexer_1_out[0]),
    .B1(multiplexer_1_out[1]), .B2(multiplexer_1_out[2]), .B3(multiplexer_1_out[3]), .A4(A[4]), .A5(A[5]),
    .A6(A[6]), .A7(A[7]), .B4(multiplexer_1_out[4]), .B5(multiplexer_1_out[5]), .B6(multiplexer_1_out[6]),
    .B7(multiplexer_1_out[7]), .S0(Diff[0]), .S1(Diff[1]), .S2(Diff[2]), .S3(Diff[3]), .S4(Diff[4]),
    .S5(Diff[5]), .S6(Diff[6]), .S7(Diff[7]), .OverflowFlag(cla_1_overflowflag));
  and and_1 (OFflag, cla_1_overflowflag, not_2_out);
endmodule
